// Logisim project 16BitCarrySelectAdder.circ as structural Verilog: 21 circuits, main circuit sixteenbitcarryselect
module sixteenbitcarryselect (
  input  [15:0] a,
  input  [15:0] b,
  input  op,
  output [15:0] S,
  output Cout
);

  wire eightbitadder0_1_cout, eightbitadder0_2_cout, eightbitadder1_1_cout;
  wire [7:0] eightbitadder0_1_s, eightbitadder1_1_s;
  wire [15:0] adder_1_out, multiplexer_1_out, not_1_out;

  Adder #(.width(16)) adder_1 (.a({16{1'b0}}), .b(not_1_out), .out(adder_1_out), .cin(op));  // open: cout
  assign not_1_out = ~b;  // NOT_Gate not_1, 16 bits wide
  Multiplexer #(.width(16)) multiplexer_1 (.in0(b), .in1(adder_1_out), .out(multiplexer_1_out), .sel(op));
  EightBitAdder1 eightbitadder1_1 (
    .a(a[15:8]), .b(multiplexer_1_out[15:8]), .S(eightbitadder1_1_s), .Cout(eightbitadder1_1_cout));
  EightBitAdder0 eightbitadder0_1 (
    .a(a[15:8]), .b(multiplexer_1_out[15:8]), .S(eightbitadder0_1_s), .Cout(eightbitadder0_1_cout));
  Multiplexer #(.width(8)) multiplexer_2 (
    .in0(eightbitadder0_1_s), .in1(eightbitadder1_1_s), .out(S[15:8]), .sel(eightbitadder0_2_cout));
  Multiplexer multiplexer_3 (
    .in0(eightbitadder0_1_cout), .in1(eightbitadder1_1_cout), .out(Cout), .sel(eightbitadder0_2_cout));
  EightBitAdder0 eightbitadder0_2 (.a(a[7:0]), .b(multiplexer_1_out[7:0]), .S(S[7:0]), .Cout(eightbitadder0_2_cout));

  // Notes on the sheet:
  //   10.5
  //   10.5
  //   10.5
  //   10.5
  //   13
  //   10.5
  //   13
  //   13
  //   13
  //   16BitCarrySelectAdder
  //   01/15/2025
  //   Ryan Kellar
endmodule

module FA0 (
  input  a,
  input  b,
  output S,
  output Cout
);

  wire nor_1_out;

  nor nor_1 (nor_1_out, a, b);
  and and_1 (Cout, a, b);
  nor nor_2 (S, nor_1_out, Cout);

  // Notes on the sheet:
  //   Cin
  //   Ryan Kellar
  //   FA0
  //   12/9/2024
endmodule

module FourBitAdder0 (
  input  [3:0] a,
  input  [3:0] b,
  output [3:0] S,
  output Cout
);

  wire fa0_1_cout, fao1_2_cout, fao2_1_cout;

  FAO1 fao1_1 (.a(b[3]), .b(a[3]), .Cin(fao1_2_cout), .S(S[3]), .Cout(Cout));
  FAO1 fao1_2 (.a(b[2]), .b(a[2]), .Cin(fao2_1_cout), .S(S[2]), .Cout(fao1_2_cout));
  FAO2 fao2_1 (.a(b[1]), .b(a[1]), .Cin(fa0_1_cout), .Cout(fao2_1_cout), .S(S[1]));
  FA0 fa0_1 (.a(b[0]), .b(a[0]), .S(S[0]), .Cout(fa0_1_cout));

  // Notes on the sheet:
  //   If Cin < 2.75 then 4.75 else Cin + 2.00
  //   If Cin < 2.75 then 5.5 else Cin + 2.75
  //   8.75
  //   9.5
  //   6.75
  //   4.75
  //   7.5
  //   5.5
  //   Ryan Kellar
  //   FourBitAdder0
  //   01/15/2025
  //   1.75
  //   9.5
  //   8.75
  //   2.75
  //   Cin + 2.25
  //   If Cin < 2.75 then 5.5 else Cin + 2.75
endmodule

module FourBitAdder1 (
  input  [3:0] a,
  input  [3:0] b,
  output [3:0] S,
  output Cout
);

  wire fa1_1_cout, fao1_2_cout, fao1_3_cout;

  FAO1 fao1_1 (.a(b[3]), .b(a[3]), .Cin(fao1_2_cout), .S(S[3]), .Cout(Cout));
  FAO1 fao1_2 (.a(b[2]), .b(a[2]), .Cin(fao1_3_cout), .S(S[2]), .Cout(fao1_2_cout));
  FAO1 fao1_3 (.a(b[1]), .b(a[1]), .Cin(fa1_1_cout), .S(S[1]), .Cout(fao1_3_cout));
  FA1 fa1_1 (.a(b[0]), .b(a[0]), .S(S[0]), .Cout(fa1_1_cout));

  // Notes on the sheet:
  //   Ryan Kellar
  //   FourBitAdder0
  //   01/15/2025
endmodule

module FAO1 (
  input  a,
  input  b,
  input  Cin,
  output S,
  output Cout
);

  wire nand_1_out, nand_2_out, nor_1_out, nor_2_out, nor_3_out, not_1_out, not_2_out;

  nand nand_1 (nand_1_out, a, b);
  nor nor_1 (nor_1_out, a, b);
  nor nor_2 (nor_2_out, nor_1_out, not_1_out);
  not not_1 (not_1_out, nand_1_out);
  nor nor_3 (nor_3_out, nor_2_out, Cin);
  nand nand_2 (nand_2_out, nor_2_out, Cin);
  not not_2 (not_2_out, nand_2_out);
  nand nand_3 (Cout, nand_2_out, nand_1_out);
  nor nor_4 (S, nor_3_out, not_2_out);

  // Notes on the sheet:
  //   1.00
  //   0.75
  //   1.00
  //   1.00
  //   1.00
  //   1.00
  //   0.75
  //   1.00
  //   1.00
  //   Ryan Kellar
  //   12/14/2024
  //   32 transistors
  //   1.00 + 0.75 + 1.00 + 1.00 + 0.75 + 1.00 = 5.5
  //   If Cin < 2.75 then 5.5 else Cin + 2.75
  //   1.00 + 0.75 + 1.00 + 1.00 + 1.00 = 4.75
  //   If Cin < 2.75 then 4.75 else Cin + 2.00
endmodule

module FA1 (
  input  a,
  input  b,
  output S,
  output Cout
);

  wire nand_1_out;

  or or_1 (Cout, a, b);
  nand nand_1 (nand_1_out, a, b);
  nand nand_2 (S, Cout, nand_1_out);

  // Notes on the sheet:
  //   Cin
  //   Ryan Kellar
  //   FA1
  //   12/11/2024
endmodule

module EightBitAdder0 (
  input  [7:0] a,
  input  [7:0] b,
  output [7:0] S,
  output Cout
);

  wire fourbitadder0_1_cout, fourbitadder0_2_cout, fourbitadder1_1_cout;
  wire [3:0] fourbitadder0_1_s, fourbitadder1_1_s;

  FourBitAdder1 fourbitadder1_1 (.a(a[7:4]), .b(b[7:4]), .S(fourbitadder1_1_s), .Cout(fourbitadder1_1_cout));
  FourBitAdder0 fourbitadder0_1 (.a(a[7:4]), .b(b[7:4]), .S(fourbitadder0_1_s), .Cout(fourbitadder0_1_cout));
  Multiplexer #(.width(4)) multiplexer_1 (
    .in0(fourbitadder0_1_s), .in1(fourbitadder1_1_s), .out(S[7:4]), .sel(fourbitadder0_2_cout));
  Multiplexer multiplexer_2 (
    .in0(fourbitadder0_1_cout), .in1(fourbitadder1_1_cout), .out(Cout), .sel(fourbitadder0_2_cout));
  FourBitAdder0 fourbitadder0_2 (.a(a[3:0]), .b(b[3:0]), .S(S[3:0]), .Cout(fourbitadder0_2_cout));

  // Notes on the sheet:
  //   8.75
  //   9.5
  //   8.75
  //   9.5
  //   8.75
  //   9.5
  //   Ryan Kellar
  //   EightBItAdder0
  //   01/15/2025
  //   10.5
  //   10.5
endmodule

module EightBitAdder1 (
  input  [7:0] a,
  input  [7:0] b,
  output [7:0] S,
  output Cout
);

  wire fourbitadder0_1_cout, fourbitadder1_1_cout, fourbitadder1_2_cout;
  wire [3:0] fourbitadder0_1_s, fourbitadder1_1_s;

  FourBitAdder1 fourbitadder1_1 (.a(a[7:4]), .b(b[7:4]), .S(fourbitadder1_1_s), .Cout(fourbitadder1_1_cout));
  FourBitAdder0 fourbitadder0_1 (.a(a[7:4]), .b(b[7:4]), .S(fourbitadder0_1_s), .Cout(fourbitadder0_1_cout));
  Multiplexer #(.width(4)) multiplexer_1 (
    .in0(fourbitadder0_1_s), .in1(fourbitadder1_1_s), .out(S[7:4]), .sel(fourbitadder1_2_cout));
  Multiplexer multiplexer_2 (
    .in0(fourbitadder0_1_cout), .in1(fourbitadder1_1_cout), .out(Cout), .sel(fourbitadder1_2_cout));
  FourBitAdder1 fourbitadder1_2 (.a(a[3:0]), .b(b[3:0]), .S(S[3:0]), .Cout(fourbitadder1_2_cout));

  // Notes on the sheet:
  //   Ryan Kellar
  //   EightBitAdder1
  //   01/15/2025
endmodule

module mx2i (
  input  in0,
  input  s0,
  input  in1,
  output z
);

  wire transmission_1_p3, transmission_1_p4;

  // Transmission_Gate transmission_1: pin names not known; wires that end beside it: in0, s0, transmission_1_p3, transmission_1_p4
  not not_1 (transmission_1_p3, s0);
  // Transmission_Gate transmission_2: pin names not known; wires that end beside it: in1, transmission_1_p3, s0, transmission_1_p4
  not not_2 (z, transmission_1_p4);

  // Notes on the sheet:
  //   2-1 Transmission Multiplexer
  //   01/08/2025
  //   Ryan Kellar
endmodule

module mx4i (
  input  d00,
  input  d01,
  input  d10,
  input  s1,
  input  d11,
  input  s0,
  output O
);

  wire mx2i_1_z, mx2i_2_z;

  mx2i mx2i_1 (.s0(s0), .in1(d01), .in0(d00), .z(mx2i_1_z));
  mx2i mx2i_2 (.s0(s0), .in1(d11), .in0(d10), .z(mx2i_2_z));
  mx2i mx2i_3 (.s0(s1), .in1(mx2i_2_z), .in0(mx2i_1_z), .z(O));

  // Notes on the sheet:
  //   4-1 Transmission Multiplexer
  //   01/08/2025
  //   Ryan Kellar
  //   z = max(d00+2, d01+2, d10+2, d11+2, s0+2.75, s1+1.75)
endmodule

module FAO2 (
  input  a,
  input  b,
  input  Cin,
  output S,
  output Cout
);

  wire and_1_out, nand_1_out, nand_2_out, nand_3_out, nor_1_out, nor_2_out, nor_3_out, not_1_out;

  nor nor_1 (nor_1_out, a, b);
  not not_1 (not_1_out, nand_1_out);
  nand nand_1 (nand_1_out, a, b);
  nor nor_2 (nor_2_out, nor_1_out, not_1_out);
  nand nand_2 (nand_2_out, a, Cin);
  nand nand_3 (nand_3_out, b, Cin);
  nor nor_3 (nor_3_out, nor_2_out, Cin);
  and and_1 (and_1_out, nor_2_out, Cin);
  nand nand_4 (Cout, nand_1_out, nand_2_out, nand_3_out);
  nor nor_4 (S, nor_3_out, and_1_out);

  // Notes on the sheet:
  //   1.00
  //   1.00
  //   1.00
  //   0.75
  //   1.00
  //   1.75
  //   1.00
  //   1.25
  //   1.00
  //   1.00
  //   Ryan Kellar
  //   12/14/2024
  //   42 transistors
  //   1.00 + 0.75 + 1.00 + 1.75 + 1.00 = 5.5
  //   If Cin < 2.75 then 5.5 else Cin + 2.75
  //   1.00 + 1.25 = 2.25
  //   Cin + 2.25
endmodule

module AddSubtractL (
  input  OP,
  input  [15:0] A,
  input  [15:0] B,
  output [15:0] S,
  output Cout
);

  Adder #(.width(16)) adder_1 (.a(A), .b(B), .out(S), .cin(OP), .cout(Cout));
endmodule

module FourBitCLA (
  input  [3:0] A,
  input  [3:0] B,
  input  C0,
  output C1,
  output C2,
  output C3,
  output C4
);

  wire and_1_out, and_2_out, and_3_out, and_4_out, G0_out, G1_out, G2_out, G3_out, P0_out, P1_out, P2_out,
       P3_out;

  and and_1 (and_1_out, P0_out, C0);
  and G0 (G0_out, A[0], B[0]);
  xor P0 (P0_out, A[0], B[0]);
  or or_1 (C1, G0_out, and_1_out);
  and and_2 (and_2_out, C1, P1_out);
  xor P1 (P1_out, A[1], B[1]);
  and G1 (G1_out, A[1], B[1]);
  xor P2 (P2_out, A[2], B[2]);
  and G2 (G2_out, A[2], B[2]);
  or or_2 (C2, and_2_out, G1_out);
  and and_3 (and_3_out, C2, P2_out);
  and and_4 (and_4_out, C3, P3_out);
  xor P3 (P3_out, A[3], B[3]);
  and G3 (G3_out, A[3], B[3]);
  or or_3 (C3, and_3_out, G2_out);
  or or_4 (C4, and_4_out, G3_out);
endmodule

module GenPropCircuitCLA (
  input  G0,
  input  P0,
  input  G1,
  input  P1,
  input  G2,
  input  P2,
  input  G3,
  input  P3,
  input  C0,
  output C4
);

  wire and_1_out, and_2_out, and_3_out, and_4_out;

  and and_1 (and_1_out, G0, P1, P2, P3);
  and and_2 (and_2_out, P0, P1, P2, P3, C0);
  and and_3 (and_3_out, G1, P2, P3);
  and and_4 (and_4_out, G2, P3);
  or or_1 (C4, and_1_out, and_2_out, and_3_out, and_4_out, G3);
endmodule

module GenPropCircuitCLAOpt (
  input  G0,
  input  P0,
  input  C0,
  input  G1,
  input  P1,
  input  G2,
  input  P2,
  input  G3,
  input  P3,
  output C4
);

  wire nand_1_out, nand_2_out, nand_3_out, nand_4_out, nand_5_out, nand_6_out, nand_7_out, nor_1_out,
       nor_2_out, not_1_out, not_2_out, not_3_out;

  not not_1 (not_1_out, P1);
  nand nand_1 (nand_1_out, P2, P3);
  nor nor_1 (nor_1_out, not_1_out, nand_1_out);
  not not_2 (not_2_out, nand_1_out);
  nand nand_2 (nand_2_out, P0, C0, nor_1_out);
  nand nand_3 (nand_3_out, nor_1_out, G0);
  nand nand_4 (nand_4_out, P3, G2);
  nand nand_5 (nand_5_out, G1, not_2_out);
  not not_3 (not_3_out, G3);
  nand nand_6 (nand_6_out, nand_2_out, nand_4_out);
  nand nand_7 (nand_7_out, nand_5_out, nand_3_out, not_3_out);
  nor nor_2 (nor_2_out, nand_6_out, nand_7_out);
  not not_4 (C4, nor_2_out);
endmodule

module AOI21 (
  input  in_1,
  input  in_2,
  input  in_3,
  output out_4
);

  wire and_1_out;

  and and_1 (and_1_out, in_1, in_2);
  nor nor_1 (out_4, and_1_out, in_3);
endmodule

module CLA3 (
  input  G0,
  input  P0,
  input  C0,
  input  G1,
  input  P1,
  input  G2,
  input  P2,
  input  G3,
  input  P3,
  output C4
);

  wire and_1_out, and_2_out, nand_1_out, nand_2_out, nand_3_out, nand_4_out, nor_1_out, nor_2_out, nor_3_out,
       nor_4_out, not_1_out, not_2_out, not_3_out, not_4_out;

  not not_1 (not_1_out, P1);
  nand nand_1 (nand_1_out, P2, P3);
  nor nor_1 (nor_1_out, not_1_out, nand_1_out);
  and and_1 (and_1_out, P0, nor_1_out);
  nand nand_2 (nand_2_out, nor_1_out, G0);
  nand nand_3 (nand_3_out, P3, G2);
  not not_2 (not_2_out, G1);
  nor nor_2 (nor_2_out, not_2_out, nand_1_out);
  not not_3 (not_3_out, G3);
  nand nand_4 (nand_4_out, nand_2_out, not_3_out, nand_3_out);
  nor nor_3 (nor_3_out, nand_4_out, nor_2_out);
  and and_2 (and_2_out, and_1_out, C0);
  not not_4 (not_4_out, nor_3_out);
  nor nor_4 (nor_4_out, and_2_out, not_4_out);
  not not_5 (C4, nor_4_out);
endmodule

module CLA4 (
  input  G0,
  input  P0,
  input  C0,
  input  G1,
  input  P1,
  input  G2,
  input  P2,
  input  G3,
  input  P3,
  output C4
);

  wire and_1_out, nand_1_out, nand_2_out, nand_3_out, nand_4_out, nor_1_out, nor_2_out, nor_3_out, not_1_out,
       not_2_out, not_3_out, not_4_out, transistor_1_out, transistor_2_out, transistor_3_out;

  not not_1 (not_1_out, P1);
  nand nand_1 (nand_1_out, P2, P3);
  nor nor_1 (nor_1_out, not_1_out, nand_1_out);
  and and_1 (and_1_out, P0, nor_1_out);
  nand nand_2 (nand_2_out, nor_1_out, G0);
  nand nand_3 (nand_3_out, P3, G2);
  not not_2 (not_2_out, G1);
  nor nor_2 (nor_2_out, not_2_out, nand_1_out);
  not not_3 (not_3_out, G3);
  nand nand_4 (nand_4_out, nand_2_out, not_3_out, nand_3_out);
  nor nor_3 (nor_3_out, nand_4_out, nor_2_out);
  Transistor #(.\type ("n")) transistor_1 (.in(transistor_2_out), .out(transistor_1_out), .gate(and_1_out));
  Transistor #(.\type ("n")) transistor_2 (.in(1'b0), .out(transistor_2_out), .gate(C0));
  not not_4 (not_4_out, nor_3_out);
  Transistor transistor_3 (.in(1'b1), .out(transistor_3_out), .gate(C0));
  Transistor transistor_4 (.in(1'b1), .out(transistor_3_out), .gate(and_1_out));
  Transistor transistor_5 (.in(transistor_3_out), .out(transistor_1_out), .gate(not_4_out));
  Transistor #(.\type ("n")) transistor_6 (.in(1'b0), .out(transistor_1_out), .gate(not_4_out));
  Transistor transistor_7 (.in(1'b1), .out(C4), .gate(transistor_1_out));
  Transistor #(.\type ("n")) transistor_8 (.in(1'b0), .out(C4), .gate(transistor_1_out));
endmodule

module GenPropCircultCLAOptL (
  input  G0,
  input  P0,
  input  C0,
  input  G1,
  input  P1,
  input  G2,
  input  P2,
  input  G3,
  input  P3,
  output C4
);

  wire nand_1_out, nand_2_out, nand_3_out, nand_4_out, nand_5_out, nand_6_out, nand_7_out, nor_1_out,
       nor_2_out, not_1_out, not_2_out, not_3_out;

  not not_1 (not_1_out, P1);
  nand nand_1 (nand_1_out, P2, P3);
  nor nor_1 (nor_1_out, not_1_out, nand_1_out);
  not not_2 (not_2_out, nand_1_out);
  nand nand_2 (nand_2_out, P0, C0, nor_1_out);
  nand nand_3 (nand_3_out, nor_1_out, G0);
  nand nand_4 (nand_4_out, P3, G2);
  nand nand_5 (nand_5_out, G1, not_2_out);
  not not_3 (not_3_out, G3);
  nand nand_6 (nand_6_out, nand_2_out, nand_4_out);
  nand nand_7 (nand_7_out, nand_5_out, nand_3_out, not_3_out);
  nor nor_2 (nor_2_out, nand_6_out, nand_7_out);
  not not_4 (C4, nor_2_out);

  // Notes on the sheet:
  //   2
  //   1
  //   3.25
  //   4.25
  //   5.25
  //   6
  //   6
endmodule

module SixteenBitAddSubtract (
  input  [15:0] a,
  input  [15:0] b,
  input  op,
  output overflow,
  output [15:0] S
);

  determiningoverflow determiningoverflow_1 (.A(a[15]), .B(b[15]), .R(S[15]), .op(op), .overflow(overflow));
  sixteenbitcarryselect sixteenbitcarryselect_1 (.a(a), .b(b), .op(op), .S(S));  // open: Cout
endmodule

module determiningoverflow (
  input  A,
  input  B,
  input  R,
  input  op,
  output overflow
);

  wire multiplexer_1_out, not_1_out, not_2_out, xor_1_out, xor_2_out;

  not not_1 (not_1_out, B);
  Multiplexer multiplexer_1 (.in0(B), .in1(not_1_out), .out(multiplexer_1_out), .sel(op));
  xor xor_1 (xor_1_out, A, multiplexer_1_out);
  not not_2 (not_2_out, xor_1_out);
  xor xor_2 (xor_2_out, multiplexer_1_out, R);
  and and_1 (overflow, not_2_out, xor_2_out);
endmodule
