// Logisim project FA.circ as structural Verilog: 5 circuits, main circuit main
module main (
  input  b,
  input  a,
  input  Cin,
  input  XORa,
  input  XORb,
  output FA0Cout,
  output FA1Cout,
  output FAO1Cout,
  output FAO2Cout,
  output FA0S,
  output FA1S,
  output FAO1S,
  output FAO2S,
  output C1,
  output C2
);

  wire and_1_out, nand_1_out, nand_2_out, nor_1_out, not_1_out, not_2_out;

  FA0 fa0_1 (.a(a), .b(b), .S(FA0S), .Cout(FA0Cout));
  not not_1 (not_1_out, XORa);
  nand nand_1 (nand_1_out, not_1_out, XORb);
  nand nand_2 (nand_2_out, XORa, not_2_out);
  not not_2 (not_2_out, XORb);
  nor nor_1 (nor_1_out, XORa, XORb);
  and and_1 (and_1_out, XORa, XORb);
  nand nand_3 (C1, nand_1_out, nand_2_out);
  nor nor_2 (C2, nor_1_out, and_1_out);
  // FA1 fa1_1: pin names not known; wires that end beside it: FA1Cout, b, a
  // FAOpt1 faopt1_1: pin names not known; wires that end beside it: FAO1Cout, b, a, Cin
  // FAOpt2 faopt2_1: pin names not known; wires that end beside it: FAO2Cout, b, FAO2S, a, Cin

  // Notes on the sheet:
  //   Distribute !(AB) to (A+B) on left side
  //   X!X is X AND NOT X, which is false (0) always
  //   Rearrange: X+Y=Y+X and XY=YX
  //   SHOWING XOR EQUIVALENCE:
  //   Distribute Outside !
  //   Distribute ! in !(AB) on left side
  //   Distribute A and B to their !A + B
  //   !( !(!AB)!(A!B) )   =   !( !(A+B)+AB )
  //   !AB + A!B   =   (A+B)!(AB)
  //   !AB + A!B   =   A!(AB) + B!(AB)
  //   !AB+A!B   =   A(!A+!B) + B(!A+!B)
  //   !AB + A!B   =   A!A + A!B + B!A + B!B
  //   !AB + A!B   =   A!B + B!A
  //   !AB + A!B   =   !AB + A!B
  //   Same equation above on the left and right sides using the DeMorgan's rules
  //   Ryan Kellar
  //   12/14/2024
  //   (using 0 for the XOR symbol)
  //   SHOWING SUM EQUIVALENCE:
  //   Use the first XOR evaluation on A 0 B
  //   Use the first XOR evaluation on the XOR C
  //   Distribute the two ! 's on the right side
  //   Distribute the A and the !B
  //   X!X is always false (right side)
  //   Distribute ! and !C
  //   Distribute the !A + B
  //   Distribute the C
  //   Rerrange (X + Y = Y + X)
  //   Same equation above on the left and right sides using the DeMorgan's rules and XOR/XNOR rules
  //   A!B!C + !AB!C + !A!BC + ABC   =   (A 0 B) 0 C
  //   A!B!C + !AB!C + !A!BC + ABC   =   (!AB + A!B) 0 C
  //   A!B!C + !AB!C + !A!BC + ABC   =   !(!AB + A!B)C + (!AB + A!B)!C
  //   A!B!C + !AB!C + !A!BC + ABC   =   ( !(!AB)!(A!B) )C + (!AB!C + A!B!C)
  //   A!B!C + !AB!C + !A!BC + ABC   =   (A + !B)(!A + B)C + !AB!C + A!B!C
  //   A!B!C + !AB!C + !A!BC + ABC   =   (AB + !A!B)C + !AB!C + A!B!C
  //   A!B!C + !AB!C + !A!BC + ABC   =   ABC + !A!BC + !AB!C + A!B!C
  //   A!B!C + !AB!C + !A!BC + ABC   =   A!B!C + !AB!C + !A!BC + ABC
  //   A!B!C + !AB!C + !A!BC + ABC   =   ( (!A + B)A + (!A+ B)!B )C + !AB!C + A!B!C
  //   A!B!C + !AB!C + !A!BC + ABC   =   (A!A + AB + !A!B + B!B)C + !AB!C + A!B!C
  //   Use the first XOR evaluation on A 0 B
  //   Use Rule 11d.: XY' + Y = X + Y with X = BC and Y = AC
  //   !(XY) = !X + !Y with X = A and Y = C
  //   X = X(Y+ !Y) with X = AC and Y = B
  //   If ABC is true, then AB is already true
  //   (using 0 for the XOR symbol)
  //   SHOWING Carry EQUIVALENCE:
  //   Distribute the C
  //   Distribute the BC
  //   X!X is always false (with X = C)
  //   Distribute the AC
  //   AB + BC + AC   =   (A 0 B)C + AB
  //   AB + BC + AC   =   !ABC + A!BC + AB
  //   Same equation above on the left and right sides using the DeMorgan's rules and XOR/XNOR rules
  //   AB + BC + AC   =   (!AB + A!B)C + AB
  //   AB + BC!(AC) + AC   =   !ABC + A!BC + AB
  //   AB + BC(!A + !C) + AC   =   !ABC + A!BC + AB
  //   AB + !ABC + BC!C + AC   =   !ABC + A!BC + AB
  //   AB + !ABC + AC   =   !ABC + A!BC + AB
  //   AB + !ABC + AC(B+!B)   =   !ABC + A!BC + AB
  //   AB + !ABC + A!BC + ABC   =   !ABC + A!BC + AB
  //   AB + !ABC + A!BC   =   !ABC + A!BC + AB
endmodule

module FA0 (
  input  a,
  input  b,
  output S,
  output Cout
);

  wire nor_1_out;

  nor nor_1 (nor_1_out, a, b);
  and and_1 (Cout, a, b);
  nor nor_2 (S, nor_1_out, Cout);

  // Notes on the sheet:
  //   Cin
  //   2.75
  //   1.75
  //   Ryan Kellar
  //   FA0
  //   12/9/2024
endmodule

module FA1 (
  input  a,
  input  b,
  output S,
  output Cout
);

  wire nand_1_out;

  or or_1 (Cout, a, b);
  nand nand_1 (nand_1_out, a, b);
  nand nand_2 (S, Cout, nand_1_out);

  // Notes on the sheet:
  //   Cin
  //   2.75
  //   1.75
  //   Ryan Kellar
  //   FA1
  //   12/11/2024
endmodule

module FAOpt1 (
  input  a,
  input  b,
  input  Cin,
  output S,
  output Cout
);

  wire nand_1_out, nand_2_out, nor_1_out, nor_2_out, nor_3_out, not_1_out, not_2_out;

  nand nand_1 (nand_1_out, a, b);
  nor nor_1 (nor_1_out, a, b);
  nor nor_2 (nor_2_out, nor_1_out, not_1_out);
  not not_1 (not_1_out, nand_1_out);
  nor nor_3 (nor_3_out, nor_2_out, Cin);
  nand nand_2 (nand_2_out, nor_2_out, Cin);
  not not_2 (not_2_out, nand_2_out);
  nand nand_3 (Cout, nand_2_out, nand_1_out);
  nor nor_4 (S, nor_3_out, not_2_out);

  // Notes on the sheet:
  //   1.00
  //   0.75
  //   1.00
  //   1.00
  //   1.00
  //   1.00
  //   0.75
  //   1.00
  //   1.00
  //   Ryan Kellar
  //   12/14/2024
  //   32 transistors
  //   1.00 + 0.75 + 1.00 + 1.00 + 0.75 + 1.00 = 5.5
  //   If Cin < 2.75 then 5.5 else Cin + 2.75
  //   1.00 + 0.75 + 1.00 + 1.00 + 1.00 = 4.75
  //   If Cin < 2.75 then 4.75 else Cin + 2.00
endmodule

module FAOpt2 (
  input  a,
  input  b,
  input  Cin,
  output S,
  output Cout
);

  wire and_1_out, nand_1_out, nand_2_out, nand_3_out, nor_1_out, nor_2_out, nor_3_out, not_1_out;

  nor nor_1 (nor_1_out, a, b);
  not not_1 (not_1_out, nand_1_out);
  nand nand_1 (nand_1_out, a, b);
  nor nor_2 (nor_2_out, nor_1_out, not_1_out);
  nand nand_2 (nand_2_out, a, Cin);
  nand nand_3 (nand_3_out, a, Cin);
  nor nor_3 (nor_3_out, nor_2_out, Cin);
  and and_1 (and_1_out, nor_2_out, Cin);
  nand nand_4 (Cout, nand_1_out, nand_2_out, nand_3_out);
  nor nor_4 (S, nor_3_out, and_1_out);

  // Notes on the sheet:
  //   1.00
  //   1.00
  //   1.00
  //   0.75
  //   1.00
  //   1.75
  //   1.00
  //   1.25
  //   1.00
  //   1.00
  //   Ryan Kellar
  //   12/14/2024
  //   42 transistors
  //   1.00 + 0.75 + 1.00 + 1.75 + 1.00 = 5.5
  //   If Cin < 2.75 then 5.5 else Cin + 2.75
  //   1.00 + 1.25 = 2.25
  //   Cin + 2.25
endmodule
