// Logisim project FourBitRippleCarryAdder.circ as structural Verilog: 3 circuits, main circuit main
module main (
  input  [3:0] a,
  input  [3:0] b,
  input  Cin,
  output [3:0] S,
  output Cout
);

  wire fao1_1_cout, fao2_2_cout, fao2_3_cout;

  FAO2 fao2_1 (.b(a[3]), .Cin(fao2_2_cout), .a(b[3]), .Cout(Cout), .S(S[3]));
  FAO2 fao2_2 (.b(a[2]), .Cin(fao2_3_cout), .a(b[2]), .Cout(fao2_2_cout), .S(S[2]));
  FAO2 fao2_3 (.b(a[1]), .Cin(fao1_1_cout), .a(b[1]), .Cout(fao2_3_cout), .S(S[1]));
  FAO1 fao1_1 (.a(b[0]), .b(a[0]), .Cin(Cin), .S(S[0]), .Cout(fao1_1_cout));

  // Notes on the sheet:
  //   Ryan Kellar
  //   12/16/2024
endmodule

module FAO1 (
  input  a,
  input  b,
  input  Cin,
  output S,
  output Cout
);

  wire nand_1_out, nand_2_out, nor_1_out, nor_2_out, nor_3_out, not_1_out, not_2_out;

  nand nand_1 (nand_1_out, a, b);
  nor nor_1 (nor_1_out, a, b);
  not not_1 (not_1_out, nand_1_out);
  nor nor_2 (nor_2_out, nor_1_out, not_1_out);
  nor nor_3 (nor_3_out, nor_2_out, Cin);
  not not_2 (not_2_out, nand_2_out);
  nand nand_2 (nand_2_out, nor_2_out, Cin);
  nor nor_4 (S, nor_3_out, not_2_out);
  nand nand_3 (Cout, nand_2_out, nand_1_out);

  // Notes on the sheet:
  //   Ryan Kellar
  //   12/14/2024
  //   32 transistors
endmodule

module FAO2 (
  input  a,
  input  b,
  input  Cin,
  output S,
  output Cout
);

  wire and_1_out, nand_1_out, nand_2_out, nand_3_out, nor_1_out, nor_2_out, nor_3_out, not_1_out;

  nor nor_1 (nor_1_out, a, b);
  not not_1 (not_1_out, nand_1_out);
  nand nand_1 (nand_1_out, a, b);
  nor nor_2 (nor_2_out, nor_1_out, not_1_out);
  nor nor_3 (nor_3_out, nor_2_out, Cin);
  and and_1 (and_1_out, nor_2_out, Cin);
  nand nand_2 (nand_2_out, a, Cin);
  nand nand_3 (nand_3_out, a, Cin);
  nor nor_4 (S, nor_3_out, and_1_out);
  nand nand_4 (Cout, nand_1_out, nand_2_out, nand_3_out);

  // Notes on the sheet:
  //   Ryan Kellar
  //   12/14/2024
  //   42 transistors
endmodule
