// Logisim project FourInputSOP7Segment.circ as structural Verilog: 1 circuit, main circuit main
module main (
  input  W,
  input  X,
  input  Y,
  input  Z
);

  wire nand_1_out, nand_2_out, nand_3_out, nand_4_out, nand_5_out, nand_6_out, nand_7_out, nand_8_out,
       nand_9_out, nand_10_out, nand_11_out, nand_12_out, nand_13_out, nand_14_out, nor_1_out, not_1_out,
       not_2_out, not_3_out, not_4_out;

  not not_1 (not_1_out, W);
  not not_2 (not_2_out, X);
  not not_3 (not_3_out, Y);
  not not_4 (not_4_out, Z);
  nand nand_1 (nand_1_out, X, not_3_out, not_4_out);
  nand nand_2 (nand_2_out, not_1_out, not_2_out, not_3_out, Z);
  nand nand_3 (nand_3_out, X, not_3_out, Z);
  nand nand_4 (nand_4_out, X, Y, not_4_out);
  nor nor_1 (nor_1_out, X, not_3_out, Z);
  nand nand_5 (nand_5_out, X, Y, Z);
  nand nand_6 (nand_6_out, not_2_out, Y);
  nand nand_7 (nand_7_out, Y, Z);
  nand nand_8 (nand_8_out, not_1_out, not_2_out, not_3_out);
  nand nand_9 (nand_9_out, nand_1_out, nand_2_out);
  nand nand_10 (nand_10_out, nand_3_out, nand_4_out);
  nand nand_11 (nand_11_out, nand_1_out, nand_2_out, nand_5_out);
  nand nand_12 (nand_12_out, nand_1_out, not_4_out);
  nand nand_13 (nand_13_out, nand_6_out, nand_2_out, nand_7_out);
  nand nand_14 (nand_14_out, nand_8_out, nand_5_out);
  _7_Segment_Display #(.active("false"), .decimalPoint("false")) u_7_segment_display_1 (
    .g(nand_14_out), .f(nand_13_out), .a(nand_9_out), .b(nand_10_out), .e(nand_12_out), .d(nand_11_out),
    .c(nor_1_out));
endmodule
