// Logisim project Mux.circ as structural Verilog: 5 circuits, main circuit main
module main (
  input  in_1,
  input  in_2,
  input  in_3,
  input  in_4,
  input  in_5,
  input  in_6,
  output logO,
  output trO
);

  LogicMux41 logicmux41_1 (.d00(in_1), .d01(in_2), .d10(in_3), .d11(in_4), .s0(in_6), .s1(in_5), .O(logO));
  TransmissionMux41 transmissionmux41_1 (.d00(in_1), .d01(in_2), .d10(in_3), .d11(in_4), .s0(in_6), .s1(in_5), .O(trO));

  // Notes on the sheet:
  //   Transmission 4-1 Mux
  //   Logic 4-1 Mux
endmodule

module LogicMux21 (
  input  in0,
  input  s,
  input  in1,
  output z
);

  wire nand_1_out, nand_2_out, not_1_out;

  not not_1 (not_1_out, s);
  nand nand_1 (nand_1_out, in0, not_1_out);
  nand nand_2 (nand_2_out, in1, s);
  nand nand_3 (z, nand_1_out, nand_2_out);

  // Notes on the sheet:
  //   2-1 Logic Multiplexer
  //   01/08/2025
  //   Ryan Kellar
  //   z = max(in0+2, s+2.75, in1+2)
endmodule

module TransmissionMux21 (
  input  in0,
  input  s0,
  input  in1,
  output z
);

  wire not_1_out, transmission_1_p4;

  not not_1 (not_1_out, s0);
  // Transmission_Gate transmission_1: pin names not known; wires that end beside it: in0, s0, not_1_out, transmission_1_p4
  not not_2 (z, transmission_1_p4);
  // Transmission_Gate transmission_2: pin names not known; wires that end beside it: in1, not_1_out, s0, transmission_1_p4

  // Notes on the sheet:
  //   2-1 Transmission Multiplexer
  //   01/08/2025
  //   Ryan Kellar
  //   z = max(in0+1, s+1.75, in1+1)
endmodule

module LogicMux41 (
  input  d00,
  input  d01,
  input  d10,
  input  d11,
  input  s0,
  input  s1,
  output O
);

  wire logicmux21_1_z, logicmux21_2_z;

  LogicMux21 logicmux21_1 (.in0(d00), .s(s0), .in1(d01), .z(logicmux21_1_z));
  LogicMux21 logicmux21_2 (.in0(d10), .s(s0), .in1(d11), .z(logicmux21_2_z));
  LogicMux21 logicmux21_3 (.in0(logicmux21_1_z), .s(s1), .in1(logicmux21_2_z), .z(O));

  // Notes on the sheet:
  //   4-1 Logic Multiplexer
  //   01/08/2025
  //   Ryan Kellar
  //   z = max(d00+4, d01+4, d10+4, d11+4, s0+4.75, s1+2.75)
endmodule

module TransmissionMux41 (
  input  d00,
  input  d01,
  input  d10,
  input  s1,
  input  d11,
  input  s0,
  output O
);

  wire transmissionmux21_1_z, transmissionmux21_2_z;

  TransmissionMux21 transmissionmux21_1 (.in0(d00), .s0(s0), .in1(d01), .z(transmissionmux21_1_z));
  TransmissionMux21 transmissionmux21_2 (.in0(d10), .s0(s0), .in1(d11), .z(transmissionmux21_2_z));
  TransmissionMux21 transmissionmux21_3 (.in0(transmissionmux21_1_z), .s0(s1), .in1(transmissionmux21_2_z), .z(O));

  // Notes on the sheet:
  //   4-1 Transmission Multiplexer
  //   01/08/2025
  //   Ryan Kellar
  //   z = max(d00+2, d01+2, d10+2, d11+2, s0+2.75, s1+1.75)
endmodule
