// Logisim project Registers.circ as structural Verilog: 18 circuits, main circuit R0R1
module R0R1 (
  input  in_1,
  input  [15:0] D,
  input  op,
  output [15:0] out_4
);

  wire clk;
  wire [15:0] R0_q, R1_q;

  Clock clock_1 (.out(clk));
  Register #(.width(16)) R0 (.D(out_4), .en(1'b1), .clk(clk), .Q(R0_q), .clr(in_1));
  Register #(.width(16)) R1 (.D(D), .en(1'b1), .clk(clk), .Q(R1_q), .clr(in_1));
  SixteenBitAddSubtract sixteenbitaddsubtract_1 (.a(R0_q), .b(R1_q), .op(op), .S(out_4));  // open: overflow

  // Other names for the same wires on the sheet: rst = in_1
endmodule

module SixteenBitAddSubtract (
  input  [15:0] a,
  input  [15:0] b,
  input  op,
  output overflow,
  output [15:0] S
);

  determiningoverflow determiningoverflow_1 (.A(a[15]), .B(b[15]), .R(S[15]), .op(op), .overflow(overflow));
  sixteenbitcarryselect sixteenbitcarryselect_1 (.a(a), .b(b), .op(op), .S(S));  // open: Cout
endmodule

module sixteenbitcarryselect (
  input  [15:0] a,
  input  [15:0] b,
  input  op,
  output [15:0] S,
  output Cout
);

  wire eightbitadder0_1_cout, eightbitadder0_2_cout, eightbitadder1_1_cout;
  wire [7:0] eightbitadder0_1_s, eightbitadder1_1_s;
  wire [15:0] adder_1_out, multiplexer_1_out, not_1_out;

  Adder #(.width(16)) adder_1 (.a({16{1'b0}}), .b(not_1_out), .out(adder_1_out), .cin(op));  // open: cout
  assign not_1_out = ~b;  // NOT_Gate not_1, 16 bits wide
  Multiplexer #(.width(16)) multiplexer_1 (.in0(b), .in1(adder_1_out), .out(multiplexer_1_out), .sel(op));
  EightBitAdder1 eightbitadder1_1 (
    .a(a[15:8]), .b(multiplexer_1_out[15:8]), .S(eightbitadder1_1_s), .Cout(eightbitadder1_1_cout));
  EightBitAdder0 eightbitadder0_1 (
    .a(a[15:8]), .b(multiplexer_1_out[15:8]), .S(eightbitadder0_1_s), .Cout(eightbitadder0_1_cout));
  Multiplexer #(.width(8)) multiplexer_2 (
    .in0(eightbitadder0_1_s), .in1(eightbitadder1_1_s), .out(S[15:8]), .sel(eightbitadder0_2_cout));
  Multiplexer multiplexer_3 (
    .in0(eightbitadder0_1_cout), .in1(eightbitadder1_1_cout), .out(Cout), .sel(eightbitadder0_2_cout));
  EightBitAdder0 eightbitadder0_2 (.a(a[7:0]), .b(multiplexer_1_out[7:0]), .S(S[7:0]), .Cout(eightbitadder0_2_cout));

  // Notes on the sheet:
  //   10.5
  //   10.5
  //   10.5
  //   10.5
  //   13
  //   10.5
  //   13
  //   13
  //   13
  //   16BitCarrySelectAdder
  //   01/15/2025
  //   Ryan Kellar
endmodule

module FA0 (
  input  a,
  input  b,
  output S,
  output Cout
);

  wire nor_1_out;

  nor nor_1 (nor_1_out, a, b);
  and and_1 (Cout, a, b);
  nor nor_2 (S, nor_1_out, Cout);

  // Notes on the sheet:
  //   Cin
  //   Ryan Kellar
  //   FA0
  //   12/9/2024
endmodule

module FourBitAdder0 (
  input  [3:0] a,
  input  [3:0] b,
  output [3:0] S,
  output Cout
);

  wire fa0_1_cout, fao1_2_cout, fao2_1_cout;

  FAO1 fao1_1 (.a(b[3]), .b(a[3]), .Cin(fao1_2_cout), .S(S[3]), .Cout(Cout));
  FAO1 fao1_2 (.a(b[2]), .b(a[2]), .Cin(fao2_1_cout), .S(S[2]), .Cout(fao1_2_cout));
  FAO2 fao2_1 (.a(b[1]), .b(a[1]), .Cin(fa0_1_cout), .Cout(fao2_1_cout), .S(S[1]));
  FA0 fa0_1 (.a(b[0]), .b(a[0]), .S(S[0]), .Cout(fa0_1_cout));

  // Notes on the sheet:
  //   If Cin < 2.75 then 4.75 else Cin + 2.00
  //   If Cin < 2.75 then 5.5 else Cin + 2.75
  //   8.75
  //   9.5
  //   6.75
  //   4.75
  //   7.5
  //   5.5
  //   Ryan Kellar
  //   FourBitAdder0
  //   01/15/2025
  //   1.75
  //   9.5
  //   8.75
  //   2.75
  //   Cin + 2.25
  //   If Cin < 2.75 then 5.5 else Cin + 2.75
endmodule

module FourBitAdder1 (
  input  [3:0] a,
  input  [3:0] b,
  output [3:0] S,
  output Cout
);

  wire fa1_1_cout, fao1_2_cout, fao1_3_cout;

  FAO1 fao1_1 (.a(b[3]), .b(a[3]), .Cin(fao1_2_cout), .S(S[3]), .Cout(Cout));
  FAO1 fao1_2 (.a(b[2]), .b(a[2]), .Cin(fao1_3_cout), .S(S[2]), .Cout(fao1_2_cout));
  FAO1 fao1_3 (.a(b[1]), .b(a[1]), .Cin(fa1_1_cout), .S(S[1]), .Cout(fao1_3_cout));
  FA1 fa1_1 (.a(b[0]), .b(a[0]), .S(S[0]), .Cout(fa1_1_cout));

  // Notes on the sheet:
  //   Ryan Kellar
  //   FourBitAdder0
  //   01/15/2025
endmodule

module FAO1 (
  input  a,
  input  b,
  input  Cin,
  output S,
  output Cout
);

  wire nand_1_out, nand_2_out, nor_1_out, nor_2_out, nor_3_out, not_1_out, not_2_out;

  nand nand_1 (nand_1_out, a, b);
  nor nor_1 (nor_1_out, a, b);
  nor nor_2 (nor_2_out, nor_1_out, not_1_out);
  not not_1 (not_1_out, nand_1_out);
  nor nor_3 (nor_3_out, nor_2_out, Cin);
  nand nand_2 (nand_2_out, nor_2_out, Cin);
  not not_2 (not_2_out, nand_2_out);
  nand nand_3 (Cout, nand_2_out, nand_1_out);
  nor nor_4 (S, nor_3_out, not_2_out);

  // Notes on the sheet:
  //   1.00
  //   0.75
  //   1.00
  //   1.00
  //   1.00
  //   1.00
  //   0.75
  //   1.00
  //   1.00
  //   Ryan Kellar
  //   12/14/2024
  //   32 transistors
  //   1.00 + 0.75 + 1.00 + 1.00 + 0.75 + 1.00 = 5.5
  //   If Cin < 2.75 then 5.5 else Cin + 2.75
  //   1.00 + 0.75 + 1.00 + 1.00 + 1.00 = 4.75
  //   If Cin < 2.75 then 4.75 else Cin + 2.00
endmodule

module FA1 (
  input  a,
  input  b,
  output S,
  output Cout
);

  wire nand_1_out;

  or or_1 (Cout, a, b);
  nand nand_1 (nand_1_out, a, b);
  nand nand_2 (S, Cout, nand_1_out);

  // Notes on the sheet:
  //   Cin
  //   Ryan Kellar
  //   FA1
  //   12/11/2024
endmodule

module EightBitAdder0 (
  input  [7:0] a,
  input  [7:0] b,
  output [7:0] S,
  output Cout
);

  wire fourbitadder0_1_cout, fourbitadder0_2_cout, fourbitadder1_1_cout;
  wire [3:0] fourbitadder0_1_s, fourbitadder1_1_s;

  FourBitAdder1 fourbitadder1_1 (.a(a[7:4]), .b(b[7:4]), .S(fourbitadder1_1_s), .Cout(fourbitadder1_1_cout));
  FourBitAdder0 fourbitadder0_1 (.a(a[7:4]), .b(b[7:4]), .S(fourbitadder0_1_s), .Cout(fourbitadder0_1_cout));
  Multiplexer #(.width(4)) multiplexer_1 (
    .in0(fourbitadder0_1_s), .in1(fourbitadder1_1_s), .out(S[7:4]), .sel(fourbitadder0_2_cout));
  Multiplexer multiplexer_2 (
    .in0(fourbitadder0_1_cout), .in1(fourbitadder1_1_cout), .out(Cout), .sel(fourbitadder0_2_cout));
  FourBitAdder0 fourbitadder0_2 (.a(a[3:0]), .b(b[3:0]), .S(S[3:0]), .Cout(fourbitadder0_2_cout));

  // Notes on the sheet:
  //   8.75
  //   9.5
  //   8.75
  //   9.5
  //   8.75
  //   9.5
  //   Ryan Kellar
  //   EightBItAdder0
  //   01/15/2025
  //   10.5
  //   10.5
endmodule

module EightBitAdder1 (
  input  [7:0] a,
  input  [7:0] b,
  output [7:0] S,
  output Cout
);

  wire fourbitadder0_1_cout, fourbitadder1_1_cout, fourbitadder1_2_cout;
  wire [3:0] fourbitadder0_1_s, fourbitadder1_1_s;

  FourBitAdder1 fourbitadder1_1 (.a(a[7:4]), .b(b[7:4]), .S(fourbitadder1_1_s), .Cout(fourbitadder1_1_cout));
  FourBitAdder0 fourbitadder0_1 (.a(a[7:4]), .b(b[7:4]), .S(fourbitadder0_1_s), .Cout(fourbitadder0_1_cout));
  Multiplexer #(.width(4)) multiplexer_1 (
    .in0(fourbitadder0_1_s), .in1(fourbitadder1_1_s), .out(S[7:4]), .sel(fourbitadder1_2_cout));
  Multiplexer multiplexer_2 (
    .in0(fourbitadder0_1_cout), .in1(fourbitadder1_1_cout), .out(Cout), .sel(fourbitadder1_2_cout));
  FourBitAdder1 fourbitadder1_2 (.a(a[3:0]), .b(b[3:0]), .S(S[3:0]), .Cout(fourbitadder1_2_cout));

  // Notes on the sheet:
  //   Ryan Kellar
  //   EightBitAdder1
  //   01/15/2025
endmodule

module mx2i (
  input  in0,
  input  s0,
  input  in1,
  output z
);

  wire transmission_1_p3, transmission_1_p4;

  // Transmission_Gate transmission_1: pin names not known; wires that end beside it: in0, s0, transmission_1_p3, transmission_1_p4
  not not_1 (transmission_1_p3, s0);
  // Transmission_Gate transmission_2: pin names not known; wires that end beside it: in1, transmission_1_p3, s0, transmission_1_p4
  not not_2 (z, transmission_1_p4);

  // Notes on the sheet:
  //   2-1 Transmission Multiplexer
  //   01/08/2025
  //   Ryan Kellar
endmodule

module mx4i (
  input  d00,
  input  d01,
  input  d10,
  input  s1,
  input  d11,
  input  s0,
  output O
);

  wire mx2i_1_z, mx2i_2_z;

  mx2i mx2i_1 (.s0(s0), .in1(d01), .in0(d00), .z(mx2i_1_z));
  mx2i mx2i_2 (.s0(s0), .in1(d11), .in0(d10), .z(mx2i_2_z));
  mx2i mx2i_3 (.s0(s1), .in1(mx2i_2_z), .in0(mx2i_1_z), .z(O));

  // Notes on the sheet:
  //   4-1 Transmission Multiplexer
  //   01/08/2025
  //   Ryan Kellar
  //   z = max(d00+2, d01+2, d10+2, d11+2, s0+2.75, s1+1.75)
endmodule

module FAO2 (
  input  a,
  input  b,
  input  Cin,
  output S,
  output Cout
);

  wire and_1_out, nand_1_out, nand_2_out, nand_3_out, nor_1_out, nor_2_out, nor_3_out, not_1_out;

  nor nor_1 (nor_1_out, a, b);
  not not_1 (not_1_out, nand_1_out);
  nand nand_1 (nand_1_out, a, b);
  nor nor_2 (nor_2_out, nor_1_out, not_1_out);
  nand nand_2 (nand_2_out, a, Cin);
  nand nand_3 (nand_3_out, b, Cin);
  nor nor_3 (nor_3_out, nor_2_out, Cin);
  and and_1 (and_1_out, nor_2_out, Cin);
  nand nand_4 (Cout, nand_1_out, nand_2_out, nand_3_out);
  nor nor_4 (S, nor_3_out, and_1_out);

  // Notes on the sheet:
  //   1.00
  //   1.00
  //   1.00
  //   0.75
  //   1.00
  //   1.75
  //   1.00
  //   1.25
  //   1.00
  //   1.00
  //   Ryan Kellar
  //   12/14/2024
  //   42 transistors
  //   1.00 + 0.75 + 1.00 + 1.75 + 1.00 = 5.5
  //   If Cin < 2.75 then 5.5 else Cin + 2.75
  //   1.00 + 1.25 = 2.25
  //   Cin + 2.25
endmodule

module AOI21 (
  input  in_1,
  input  in_2,
  input  in_3,
  output out_4
);

  wire and_1_out;

  and and_1 (and_1_out, in_1, in_2);
  nor nor_1 (out_4, and_1_out, in_3);
endmodule

module determiningoverflow (
  input  A,
  input  B,
  input  R,
  input  op,
  output overflow
);

  wire multiplexer_1_out, not_1_out, not_2_out, xor_1_out, xor_2_out;

  not not_1 (not_1_out, B);
  Multiplexer multiplexer_1 (.in0(B), .in1(not_1_out), .out(multiplexer_1_out), .sel(op));
  xor xor_1 (xor_1_out, A, multiplexer_1_out);
  not not_2 (not_2_out, xor_1_out);
  xor xor_2 (xor_2_out, multiplexer_1_out, R);
  and and_1 (overflow, not_2_out, xor_2_out);
endmodule

module TestRegisters (
  input  in_1,
  input  op,
  input  [1:0] Rd,
  input  [1:0] Rs,
  output [15:0] a,
  output [15:0] b,
  output [15:0] out_7,
  output [15:0] out_8,
  output [15:0] out_9,
  output [15:0] out_10
);

  wire clk, ovrfl, register_1_q, regwe_1_reg0we, regwe_1_reg1we, regwe_1_reg2we, regwe_1_reg3we;
  wire [15:0] sixteenbitaddsubtract_1_s;

  Register #(.width(1)) register_1 (.D(1'b1), .en(ovrfl), .clk(clk), .Q(register_1_q), .clr(in_1));
  Clock clock_1 (.out(clk));
  LED led_1 (.in(register_1_q));
  SixteenBitAddSubtract sixteenbitaddsubtract_1 (
    .a(a), .b(b), .op(op), .overflow(ovrfl), .S(sixteenbitaddsubtract_1_s));
  srcSel srcsel_1 (.sel(Rd), .reg0(out_7), .reg1(out_8), .reg2(out_9), .reg3(out_10), .regOut(a));
  srcSel srcsel_2 (.sel(Rs), .reg0(out_7), .reg1(out_8), .reg2(out_9), .reg3(out_10), .regOut(b));
  regWE regwe_1 (
    .Rd(Rd), .regWrite(1'b1), .reg0WE(regwe_1_reg0we), .reg1WE(regwe_1_reg1we), .reg2WE(regwe_1_reg2we),
    .reg3WE(regwe_1_reg3we));
  Register #(.width(16)) R0 (.D(sixteenbitaddsubtract_1_s), .en(regwe_1_reg0we), .clk(clk), .Q(out_7), .clr(in_1));
  Register #(.width(16)) R1 (.D(sixteenbitaddsubtract_1_s), .en(regwe_1_reg1we), .clk(clk), .Q(out_8), .clr(in_1));
  Register #(.width(16)) R2 (.D(sixteenbitaddsubtract_1_s), .en(regwe_1_reg2we), .clk(clk), .Q(out_9), .clr(in_1));
  Register #(.width(16)) R3 (.D(sixteenbitaddsubtract_1_s), .en(regwe_1_reg3we), .clk(clk), .Q(out_10), .clr(in_1));

  // Other names for the same wires on the sheet: R0[15:0] = out_7; R1[15:0] = out_8; R2[15:0] = out_9;
  //   R3[15:0] = out_10; rst = in_1
endmodule

module srcSel (
  input  [1:0] sel,
  input  [15:0] reg0,
  input  [15:0] reg1,
  input  [15:0] reg2,
  input  [15:0] reg3,
  output [15:0] regOut
);

  wire [15:0] multiplexer_1_out, multiplexer_2_out;

  Multiplexer #(.width(16)) multiplexer_1 (.in0(reg0), .in1(reg1), .out(multiplexer_1_out), .sel(sel[0]));
  Multiplexer #(.width(16)) multiplexer_2 (.in0(reg2), .in1(reg3), .out(multiplexer_2_out), .sel(sel[0]));
  Multiplexer #(.width(16)) multiplexer_3 (
    .in0(multiplexer_1_out), .in1(multiplexer_2_out), .out(regOut), .sel(sel[1]));
endmodule

module regWE (
  input  [1:0] Rd,
  input  regWrite,
  output reg0WE,
  output reg1WE,
  output reg2WE,
  output reg3WE
);

  wire not_1_out, not_2_out;

  not not_1 (not_1_out, Rd[0]);
  not not_2 (not_2_out, Rd[1]);
  and and_1 (reg0WE, not_1_out, regWrite, not_2_out);
  and and_2 (reg1WE, Rd[0], regWrite, not_2_out);
  and and_3 (reg2WE, not_1_out, regWrite, Rd[1]);
  and and_4 (reg3WE, Rd[0], regWrite, Rd[1]);
endmodule
