// Logisim project SOP7Segment.circ as structural Verilog: 1 circuit, main circuit main
module main (
  input  x3,
  input  y3,
  input  z3,
  input  x1,
  input  y1,
  input  z1,
  input  x2,
  input  y2,
  input  z2
);

  wire a1_out, a2_out, a3_out, Aa1_out, Aa2_out, and_1_out, and_2_out, and_3_out, b1_out, b2_out, b3_out,
       Ca_out, cg1_out, cg2_out, cg3_out, d1_out, d2_out, d3_out, e1_out, e2_out, e3_out, La_out, nand_1_out,
       nand_2_out, nand_3_out, not_1_out, not_2_out, not_3_out, not_4_out, not_5_out, not_6_out, not_7_out,
       not_8_out, not_9_out, Sa1_out, Sa2_out;

  not not_1 (not_1_out, x1);
  not not_2 (not_2_out, y1);
  not not_3 (not_3_out, z1);
  and La (La_out, not_1_out, not_2_out, not_3_out);
  and Aa1 (Aa1_out, not_1_out, not_2_out, z1);
  and Sa1 (Sa1_out, not_1_out, y1, not_3_out);
  and Aa2 (Aa2_out, not_1_out, y1, z1);
  and Ca (Ca_out, x1, not_2_out, not_3_out);
  and Sa2 (Sa2_out, x1, not_2_out, z1);
  or a1 (a1_out, Aa1_out, Sa1_out, Aa2_out, Ca_out, Sa2_out);
  or b1 (b1_out, Aa1_out, Aa2_out);
  or cg1 (cg1_out, Aa1_out, Sa1_out, Aa2_out, Sa2_out);
  or d1 (d1_out, La_out, Sa1_out, Ca_out, Sa2_out);
  or e1 (e1_out, La_out, Aa1_out, Aa2_out, Ca_out);
  _7_Segment_Display u_7_segment_display_1 (
    .g(cg1_out), .f(1'b1), .a(a1_out), .b(b1_out), .e(e1_out), .d(d1_out), .c(cg1_out));  // open: dp
  not not_4 (not_4_out, x2);
  not not_5 (not_5_out, y2);
  not not_6 (not_6_out, z2);
  and and_1 (and_1_out, z2, not_4_out);
  and and_2 (and_2_out, x2, not_6_out);
  and and_3 (and_3_out, not_6_out, not_5_out);
  or a2 (a2_out, x2, y2, z2);
  and b2 (b2_out, z2, not_4_out);
  or cg2 (cg2_out, z2, y2);
  or d2 (d2_out, not_6_out, x2);
  or e2 (e2_out, and_1_out, and_2_out, and_3_out);
  _7_Segment_Display u_7_segment_display_2 (
    .g(cg2_out), .f(1'b1), .a(a2_out), .b(b2_out), .e(e2_out), .d(d2_out), .c(cg2_out));  // open: dp
  not not_7 (not_7_out, x3);
  not not_8 (not_8_out, y3);
  not not_9 (not_9_out, z3);
  nand nand_1 (nand_1_out, z3, not_7_out);
  nand nand_2 (nand_2_out, x3, not_9_out);
  nand nand_3 (nand_3_out, not_9_out, not_8_out);
  nand cg3 (cg3_out, not_9_out, not_8_out);
  nand d3 (d3_out, z3, not_7_out);
  nand e3 (e3_out, nand_1_out, nand_3_out);
  nor b3 (b3_out, not_9_out, x3);
  nand a3 (a3_out, not_7_out, not_8_out, not_9_out);
  _7_Segment_Display u_7_segment_display_3 (
    .g(cg3_out), .f(1'b1), .a(a3_out), .b(b3_out), .e(e3_out), .d(d3_out), .c(cg3_out));  // open: dp

  // Notes on the sheet:
  //   58 transistors
  //   36 transistors
endmodule
