// Logisim project XBitRippleCarryAdder.circ as structural Verilog: 4 circuits, main circuit main
module main (
  input  [3:0] a4,
  input  [3:0] b4,
  input  Cin4,
  input  [7:0] a8,
  input  [7:0] b8,
  output [3:0] S4,
  output Cout4,
  output [7:0] S8,
  output Cout8
);

  wire fa0_1_cout, fao1_1_cout, fao2_2_cout, fao2_4_cout, fao2_5_cout, fao2_6_cout, fao2_7_cout, fao2_8_cout,
       fao2_9_cout, fao2_10_cout;

  FAO2 fao2_1 (.b(a4[3]), .Cin(fao2_2_cout), .a(b4[3]), .Cout(Cout4), .S(S4[3]));
  FAO2 fao2_2 (.b(a4[2]), .Cin(fao2_5_cout), .a(b4[2]), .Cout(fao2_2_cout), .S(S4[2]));
  FAO2 fao2_3 (.b(b8[7]), .Cin(fao2_4_cout), .a(a8[7]), .Cout(Cout8), .S(S8[7]));
  FAO2 fao2_4 (.b(b8[6]), .Cin(fao2_6_cout), .a(a8[6]), .Cout(fao2_4_cout), .S(S8[6]));
  FAO2 fao2_5 (.b(a4[1]), .Cin(fao1_1_cout), .a(b4[1]), .Cout(fao2_5_cout), .S(S4[1]));
  FAO2 fao2_6 (.b(b8[5]), .Cin(fao2_7_cout), .a(a8[5]), .Cout(fao2_6_cout), .S(S8[5]));
  FAO1 fao1_1 (.a(b4[0]), .b(a4[0]), .Cin(Cin4), .S(S4[0]), .Cout(fao1_1_cout));
  FAO2 fao2_7 (.b(b8[4]), .Cin(fao2_8_cout), .a(a8[4]), .Cout(fao2_7_cout), .S(S8[4]));
  FAO2 fao2_8 (.b(b8[3]), .Cin(fao2_9_cout), .a(a8[3]), .Cout(fao2_8_cout), .S(S8[3]));
  FAO2 fao2_9 (.b(b8[2]), .Cin(fao2_10_cout), .a(a8[2]), .Cout(fao2_9_cout), .S(S8[2]));
  FAO2 fao2_10 (.b(b8[1]), .Cin(fa0_1_cout), .a(a8[1]), .Cout(fao2_10_cout), .S(S8[1]));
  FA0 fa0_1 (.a(a8[0]), .b(b8[0]), .S(S8[0]), .Cout(fa0_1_cout));

  // Notes on the sheet:
  //   20.5
  //   18.25
  //   21
  //   Ryan Kellar
  //   12/16/2024
  //   4 Bit Ripple Carry Adder
  //   18.75
  //   21
  //   20.5
  //   16
  //   16.5
  //   13.75
  //   11.5
  //   14.25
  //   12
  //   Ryan Kellar
  //   12/17/2024
  //   8 Bit Ripple Carry Adder
  //   326 transistors
  //   9.25
  //   7
  //   9.75
  //   7.5
  //   4.75
  //   5.5
endmodule

module FAO1 (
  input  a,
  input  b,
  input  Cin,
  output S,
  output Cout
);

  wire nand_1_out, nand_2_out, nor_1_out, nor_2_out, nor_3_out, not_1_out, not_2_out;

  nand nand_1 (nand_1_out, a, b);
  nor nor_1 (nor_1_out, a, b);
  not not_1 (not_1_out, nand_1_out);
  nor nor_2 (nor_2_out, nor_1_out, not_1_out);
  nor nor_3 (nor_3_out, nor_2_out, Cin);
  not not_2 (not_2_out, nand_2_out);
  nand nand_2 (nand_2_out, nor_2_out, Cin);
  nor nor_4 (S, nor_3_out, not_2_out);
  nand nand_3 (Cout, nand_2_out, nand_1_out);

  // Notes on the sheet:
  //   Ryan Kellar
  //   12/14/2024
  //   32 transistors
endmodule

module FAO2 (
  input  a,
  input  b,
  input  Cin,
  output S,
  output Cout
);

  wire and_1_out, nand_1_out, nand_2_out, nand_3_out, nor_1_out, nor_2_out, nor_3_out, not_1_out;

  nor nor_1 (nor_1_out, a, b);
  not not_1 (not_1_out, nand_1_out);
  nand nand_1 (nand_1_out, a, b);
  nor nor_2 (nor_2_out, nor_1_out, not_1_out);
  nor nor_3 (nor_3_out, nor_2_out, Cin);
  and and_1 (and_1_out, nor_2_out, Cin);
  nand nand_2 (nand_2_out, b, Cin);
  nand nand_3 (nand_3_out, a, Cin);
  nor nor_4 (S, nor_3_out, and_1_out);
  nand nand_4 (Cout, nand_1_out, nand_2_out, nand_3_out);

  // Notes on the sheet:
  //   Ryan Kellar
  //   12/14/2024
  //   42 transistors
endmodule

module FA0 (
  input  a,
  input  b,
  output S,
  output Cout
);

  wire nor_1_out;

  nor nor_1 (nor_1_out, a, b);
  and and_1 (Cout, a, b);
  nor nor_2 (S, nor_1_out, Cout);

  // Notes on the sheet:
  //   Cin
  //   Ryan Kellar
  //   12/9/2024
endmodule
