// Logisim project XOR.circ as structural Verilog: 2 circuits, main circuit MyXOR
module MyXOR (
  input  a,
  input  b,
  output out_3
);

  wire and_1_out, not_1_out, or_1_out;

  and and_1 (and_1_out, a, b);
  not not_1 (not_1_out, and_1_out);
  or or_1 (or_1_out, a, b);
  and and_2 (out_3, not_1_out, or_1_out);
endmodule

module MyXORCircuit (
  input  a,
  input  b,
  input  y,
  output z
);

  wire myxor_1_out_3;

  MyXOR myxor_1 (.b(b), .a(a), .out_3(myxor_1_out_3));
  MyXOR myxor_2 (.b(y), .a(myxor_1_out_3), .out_3(z));
endmodule
